# Fritzing sketch Po_Read_SoundSensor_FC04 (saved by Fritzing 0.9.0b)

parts:
  元件1 = Arduino Uno (Rev3)
  Part1 = Breakout Board for Electret Microphone

nets:
  N1: 元件1.A5/SCL, Part1.AUD
  GND: 元件1.GND, Part1.GND
  5V: 元件1.5V, Part1.VCC

notes:
  have use LED 13
