# Fritzing sketch Po_Read_clock_ds1302 (saved by Fritzing 0.9.0b)

parts:
  元件1 = Arduino Uno (Rev3)
  IC1 = DS1302 [package="DIP8 [THT]"]

nets:
  N1: 元件1.GND, IC1.0V
  N2: 元件1.D5_PWM, IC1.CE_-_Chip_Enable
  N3: 元件1.D6_PWM, IC1.I/O_-_SPI_Data_In/Out
  N4: 元件1.D7, IC1.SCLK_-_SPI_Clock
  N5: 元件1.5V, IC1.+V

notes:
  Vcc (5v)
  GND
  RST/CE (Chip Enable)
  DAT/IO (Input/Output)
  CLK/SCL (Serial Clock)
