# Fritzing sketch Po_Read_Joystick (saved by Fritzing 0.9.0b)

parts:
  元件1 = Arduino Uno (Rev3)
  Part1 = Thumb Joystick

nets:
  N1: 元件1.A0, Part1.VERT
  N2: 元件1.A1, Part1.HORZ
  N3: 元件1.A2, Part1.SEL
  GND: 元件1.GND, Part1.GND
  5V: 元件1.5V, Part1.VCC

notes:
  X
  Y
  SW
