# Fritzing sketch Po_Read_LM35ToTemp (saved by Fritzing 0.9.0b)

parts:
  元件1 = Arduino Uno (Rev3)
  U1 = 步进电机驱动
  U2 = 步进电机

nets:
  5V: 元件1.5V, U1.VCC
  GND: 元件1.GND, U1.GND
  N1: 元件1.D2, U1.BJ1
  N2: 元件1.D3_PWM, U1.BJ2
  N3: 元件1.D4, U1.BJ3
  N4: 元件1.D5_PWM, U1.BJ4
  N5: U1.VOUT1, U2.VCC
  N6: U1.A, U2.A
  N7: U1.B, U2.B
  N8: U1.C, U2.C
  N9: U1.D, U2.D
