# Fritzing sketch Po_74HC595_ctrl_8LED (saved by Fritzing 0.9.0b)
breadboards: 1

parts:
  元件1 = Arduino Uno (Rev3)
  J1 = Piezo Speaker
  R1 = Resistor [tolerance=±5% resistance=10k package=THT]
  LED1 = LED - 5mm [color="Red (633nm)" package="5 mm [THT]"]

nets:
  N1: 元件1.A5/SCL, R1.Pin_1, LED1.cathode
  N2: 元件1.GND, J1.pin1, R1.Pin_0
  N3: 元件1.D3_PWM, J1.pin2
  N4: 元件1.5V, LED1.anode

notes:
  有源蜂鸣器
  flame sensor
