# Fritzing sketch Po_Ctrl_SG90 (saved by Fritzing 0.9.0b)
breadboards: 1

parts:
  元件1 = Arduino Uno (Rev3)
  R3 = Trimmer Potentiometer [maximum_resistance=10kΩ package=THT]
  part = Trimmer Potentiometer [maximum_resistance=10kΩ package=THT]  # not connected
  J1 = Basic Servo

nets:
  N1: 元件1.A5/SCL, R3.wiper
  GND: 元件1.GND, R3.leg2, J1.gnd
  N2: 元件1.D9_PWM, J1.pulse
  5V: 元件1.5V, R3.leg1, J1.vcc

notes:
  yellow
