# Fritzing sketch Po_Potentiometer_via_serial (saved by Fritzing 0.9.0b)
breadboards: 1

parts:
  Part1 = Arduino Uno (Rev3)
  R1 = Trimmer Potentiometer [maximum_resistance=10kΩ package=THT]

nets:
  N1: Part1.A1, R1.wiper
  N2: Part1.5V, R1.leg1
  N3: Part1.GND, R1.leg2
