# Fritzing sketch Po_PWM_Ctrl_Buzzer (saved by Fritzing 0.9.0b)
breadboards: 1

parts:
  Part1 = Arduino Uno (Rev3)
  R1 = Trimmer Potentiometer [maximum_resistance=10kΩ package=THT]
  R2 = Resistor [tolerance=±5% resistance=220 package=THT]
  LED1 = LED - 5mm [color="Red (633nm)" package="5 mm [THT]"]

nets:
  N1: Part1.A1, R1.wiper
  N2: Part1.D3_PWM, LED1.cathode
  N3: Part1.5V, R1.leg1, R2.Pin_1
  N4: Part1.GND, R1.leg2
  N5: R2.Pin_0, LED1.anode
