# Fritzing sketch Po_Seven_segment_display (saved by Fritzing 0.9.0b)
breadboards: 1

parts:
  Part1 = Arduino Uno (Rev3)
  R2 = Photocell (LDR) [package=THT]  # not connected
  R3 = Resistor [tolerance=±5% resistance=1k package=THT]

nets:
  N1: Part1.A2, R3.Pin_1
  N2: Part1.5V, R3.Pin_0
